// Logisim project 201811970CGB.circ as structural Verilog: 1 circuit, main circuit main
module main (
  input  x,
  input  y,
  output S
);

  wire and_1_out, and_2_out, clock_1_out, nand_1_out, nand_2_out, nand_3_out, nand_4_out, not_1_out,
       or_1_out, xor_1_out;

  and and_1 (and_1_out, x, y);
  nand nand_1 (nand_1_out, nand_3_out, nand_2_out);
  nand nand_2 (nand_2_out, nand_1_out, nand_4_out);
  xor xor_1 (xor_1_out, x, y);
  and and_2 (and_2_out, xor_1_out, nand_2_out);
  nand nand_3 (nand_3_out, not_1_out, clock_1_out);
  nand nand_4 (nand_4_out, clock_1_out, or_1_out);
  xor xor_2 (S, xor_1_out, nand_2_out);
  or or_1 (or_1_out, and_2_out, and_1_out);
  not not_1 (not_1_out, or_1_out);
  Clock clock_1 (.out(clock_1_out));
endmodule
